# Fritzing sketch sketch1_schem (saved by Fritzing 0.9.4)
breadboards: 1

parts:
  Part1 = Arduino Uno (Rev3)
  Q1 = NPN-Transistor [package="TO92 [THT]"]
  M1 = DC Motor
  S1 = Pushbutton [package="[THT]"]

nets:
  N1: Part1.D9_PWM, Q1.B
  N2: Part1.D12/MISO, S1.Pin_3, S1.Pin_4
  N3: Part1.GND, Q1.E, S1.Pin_1, S1.Pin_2
  N4: Part1.VIN, M1.pin_1
  N5: Q1.C, M1.pin_2
