# Fritzing sketch sketch2 (saved by Fritzing 0.9.4)
breadboards: 1

parts:
  Part1 = Arduino Uno (Rev3)
  R1 = PHOTOCELL [package=photocell]
  R2 = Resistor [tolerance=±5% resistance=10k package=THT]
  M2 = Dagu DGServo 9g (Top view) [part_number=RS001B]

nets:
  N1: Part1.A0, R1.P$1, R2.Pin_1
  N2: Part1.D9_PWM, M2.pulse
  5V: Part1.5V, R1.P$2, M2.vcc
  GND: Part1.GND, R2.Pin_0, M2.gnd
